# Fritzing sketch Tempsensor (saved by Fritzing 0.9.3b)
circuit board: 8.46667cm x 5.64444cm
breadboards: 1

parts:
  NodeMcu = NodeMCU V3.0
  DS1 = DS18B20 1-Wire Temperature Sensor [part_number=DS18B20]

nets:
  N1: NodeMcu.D1, DS1.DQ
  3V3: NodeMcu.3V3, DS1.VDD
  N2: NodeMcu.GND#6, NodeMcu.GND#13, NodeMcu.GND#16, NodeMcu.GND#33, DS1.GND

custom parts:
  NodeMCU V3.0: ESP8266 based NodeMCU
